# Fritzing sketch Stepper_Control_PCB (saved by Fritzing 0.9.3b)
circuit board: 6.93562cm x 5.18321cm
breadboards: 1

parts:
  M2 = Stepper Motor - Bipolar
  R2 = Trimmer Potentiometer [maximum_resistance=10kΩ package=THT]
  IC2 = H-Bridge [package=THT]
  IC1 = H-Bridge [package=THT]
  M3 = Stepper Motor - Bipolar
  JP6 = Header 5x2 [package=avr_icsp]
  JP7 = Header 5x2 [package=avr_icsp]
  R3 = Trimmer Potentiometer [maximum_resistance=10kΩ package=THT]

nets:
  N1: M2.A, IC1.1Y
  N2: M2.C, IC1.2Y
  N3: M2.B, IC1.4Y
  N4: M2.D, IC1.3Y
  GND1: R2.leg1, IC1.GND1, IC1.GND2, IC1.GND3, IC1.GND4, JP7.8
  N5: R2.wiper, JP7.9
  N6: R2.leg2, IC1.1_2EN, IC1.3_4EN, IC1.VCC1, JP7.6
  N7: IC2.1_2EN, IC2.3_4EN, IC2.VCC1, JP6.6, R3.leg2
  N8: IC2.1A, JP6.7
  N9: IC2.1Y, M3.A
  GND1_2: IC2.GND1, IC2.GND2, IC2.GND3, IC2.GND4, JP6.8, R3.leg1
  N10: IC2.2Y, M3.C
  N11: IC2.2A, JP6.5
  N12: IC2.VCC2, JP6.4
  N13: IC2.3A, JP6.3
  N14: IC2.3Y, M3.D
  N15: IC2.4Y, M3.B
  N16: IC2.4A, JP6.1
  N17: IC1.1A, JP7.7
  N18: IC1.2A, JP7.5
  N19: IC1.VCC2, JP7.4
  N20: IC1.3A, JP7.3
  N21: IC1.4A, JP7.1
  N22: JP6.9, R3.wiper
